# Fritzing sketch Rpi_circuit (saved by Fritzing 0.9.9b)
breadboards: 1

parts:
  Mod1 = Raspberry Pi 4B
  Composant1 = Adafruit MCP4725 Breakout Board - 12-Bit DAC [part_number="Adafruit #935"]
  Composant2 = Adafruit ADS1115 16Bit I2C ADC [part_number="Adafruit #1085"]

nets:
  VDD: Mod1.3V3, Composant1.VDD, Composant2.VDD
  N1: Mod1.GPIO2, Composant1.SDA
  N2: Mod1.GPIO3, Composant1.SCL
  GND: Mod1.GND, Composant1.GND, Composant2.GND
  N3: Mod1.GPIO22, Composant2.SDA
  N4: Mod1.GPIO9, Composant2.SCL
  N5: Composant1.VOUT, Composant2.AIN0

custom parts:
  Adafruit MCP4725 Breakout Board - 12-Bit DAC: Your microcontroller probably has an ADC (analog -> digital converter) but does it have a DAC (digital -> analog converter)??? Now it can! This breakout board features the easy-to-use MCP4725 12-bit DAC. Control it via I2C and send it the value you want it to output, and the VOUT pin will have it. Great for audio / analog projects, such as when you can't use PWM but need a sine wave or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
  Adafruit ADS1115 16Bit I2C ADC: For microcontrollers without an analog-to-digital converter or when you want a higher-precision ADC, the ADS1115 provides 16-bit precision at 860 samples/second over I2C. The chip can be configured as 4 single-ended input channels, or two differential channels. As a nice bonus, it even includes a programmable gain amplifier, up to x16, to help boost up smaller single/differential signals to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
